# Fritzing sketch AD5206_control_CD40106 (saved by Fritzing 0.9.1b)
breadboards: 1

parts:
  Composant1 = Arduino Uno (Rev3)
  IC1 = IC, DIP package, 24 pins [chip_label=AD5206]
  IC2 = IC, DIP package, 14 pins [chip_label=CD40106]
  C1 = Electrolytic Capacitor [capacitance=1µF package="100 mil [THT, electrolytic]"]
  VCC1 = Battery block 9V
  U1 = 3.5mm Audio Jack [package=audio-jack-3.5mm-smd]

nets:
  N1: Composant1.D10_PWM/SS, IC1.pin5
  N2: Composant1.D11_PWM/MOSI, IC1.pin7
  N3: Composant1.D13/SCK, IC1.pin8
  N4: Composant1.5V, IC1.pin6
  N5: Composant1.GND, IC1.pin4, IC1.pin9
  N6: IC1.pin11, IC2.pin2, U1.RIGHT
  N7: IC1.pin12, IC2.pin1, C1.-
  N8: IC2.pin7, C1.+, VCC1.-, U1.SLEEVE
  N9: IC2.pin14, VCC1.+

// code stored in the sketch: ad5206_control_CD40106.ino
/*
  Digital Pot Control
 
  This example controls an Analog Devices AD5206 digital potentiometer.
  The AD5206 has 6 potentiometer channels. Each channel's pins are labeled
  A - connect this to voltage
  W - this is the pot's wiper, which changes when you set it
  B - connect this to ground.
 
 The AD5206 is SPI-compatible,and to command it, you send two bytes,
 one with the channel number (0 - 5) and one with the resistance value for the
 channel (0 - 255).  
 
 The circuit:
  * All A pins  of AD5206 connected to +5V
  * All B pins of AD5206 connected to ground
  * An LED and a 220-ohm resisor in series connected from each W pin to ground
  * CS - to digital pin 10  (SS pin)
  * SDI - to digital pin 11 (MOSI pin)
  * CLK - to digital pin 13 (SCK pin)
 
 created 10 Aug 2010
 by Tom Igoe
 
 Thanks to Heather Dewey-Hagborg for the original tutorial, 2005
 
*/


// inslude the SPI library:
#include <SPI.h>


// set pin 10 as the slave select for the digital pot:
const int slaveSelectPin = 10;

void setup() {
  // set the slaveSelectPin as an output:
  pinMode (slaveSelectPin, OUTPUT);
  // initialize SPI:
  SPI.begin();
}

void loop() {

    // change the resistance on this channel from min to max:
    for (int level = 0; level < 255; level++) {
      digitalPotWrite(4, level);
      delay(5);
    }
    // wait a second at the top:
    delay(50);
    // change the resistance on this channel from max to min:
    for (int level = 0; level < 255; level++) {
      digitalPotWrite(4, 255 - level);
      delay(5);
    }


}

void digitalPotWrite(int address, int value) {
  // take the SS pin low to select the chip:
  digitalWrite(slaveSelectPin,LOW);
  //  send in the address and value via SPI:
  SPI.transfer(address);
  SPI.transfer(value);
  // take the SS pin high to de-select the chip:
  digitalWrite(slaveSelectPin,HIGH);
}
